# Fritzing sketch lightmashine-shield (saved by Fritzing 0.7.12b)

parts:
  light_mashine_shield = Arduino
  R2 = Resistor [tolerance=±5% resistance=220 package=THT]
  R3 = Resistor [tolerance=±5% resistance=220 package=THT]
  R4 = Resistor [tolerance=±5% resistance=220 package=THT]
  R5 = Resistor [tolerance=±5% resistance=220 package=THT]
  R6 = Resistor [tolerance=±5% resistance=220 package=THT]
  R7 = Resistor [tolerance=±5% resistance=220 package=THT]
  R8 = Resistor [tolerance=±5% resistance=220 package=THT]
  R9 = Resistor [tolerance=±5% resistance=220 package=THT]
  R10 = Resistor [tolerance=±5% resistance=220 package=THT]
  R11 = Resistor [tolerance=±5% resistance=220 package=THT]
  R12 = Resistor [tolerance=±5% resistance=220 package=THT]
  R13 = Resistor [tolerance=±5% resistance=220 package=THT]
  R14 = Resistor [tolerance=±5% resistance=220 package=THT]

nets:
  N1: light_mashine_shield.GND, R2.Pin_0
  N2: light_mashine_shield.D13, R3.Pin_0
  N3: light_mashine_shield.D12, R4.Pin_0
  N4: light_mashine_shield.D11, R5.Pin_0
  N5: light_mashine_shield.D10, R6.Pin_0
  N6: light_mashine_shield.D9, R7.Pin_0
  N7: light_mashine_shield.D8, R8.Pin_0
  N8: light_mashine_shield.D7, R9.Pin_0
  N9: light_mashine_shield.D6, R12.Pin_0
  N10: light_mashine_shield.D5, R14.Pin_0
  N11: light_mashine_shield.D4, R10.Pin_0
  N12: light_mashine_shield.D3, R13.Pin_0
  N13: light_mashine_shield.D2, R11.Pin_0
  5V: light_mashine_shield.VIN
  N14: light_mashine_shield.A0, R2.Pin_1

notes:
  AREF
  GND
  13
  12
  ~11
  ~10
  ~9
  8
  7
  ~6
  ~5
  ~3
  4
  2
  TX->1
  RX<-0
  A0
  A1
  A2
  A3
  A4
  A5
  signal
  Vin+
  5V
  3.3V
  RESET
  IOREF
  ~6.
  ~9.
